# Fritzing sketch steamakers_rgb (saved by Fritzing 0.9.9b)

parts:
  IC1 = ks0172 [chip_label=?]
  LED1 = RGB LED (com. cathode, rgb) [package="5 mm [THT]"]

nets:
  N1: IC1.12_/_MISO, LED1.blue_anode
  N2: IC1.13_/_SCK, LED1.green_anode
  N3: IC1.SDA, LED1.red_anode
  N4: IC1.GND, LED1.common_cathode

notes:
  Rojo - SDA (21)
  Azul - 19
  Verde - 18
  GND - GND

custom parts:
  ks0172: Arduino UNO R3 extra pins
